# Fritzing sketch Atari_Punk_Controller_NE556 (saved by Fritzing 0.9.3b)
circuit board: 3.3cm x 3.3cm
breadboards: 1

parts:
  Audio_Out = Audio Jack (TRS) 3.5mm [package="4Ucon 08780 [THT]"]
  NE556 = 556 [package=dil14]
  470k = female pin header, 3 pins [form="♀ (female)"]
  470k_2 = female pin header, 3 pins [form="♀ (female)"]
  10uF = Electrolytic Capacitor [capacitance=10µF package="100 mil [THT, electrolytic]"]
  1k = Resistor [tolerance=±5% resistance=220 package=THT]
  10k = Resistor [tolerance=±5% resistance=220 package=THT]
  10nF = Ceramic Capacitor [capacitance=10nF package="100 mil [THT, multilayer]"]
  100nF = Ceramic Capacitor [capacitance=10nF package="100 mil [THT, multilayer]"]
  4_7k = Resistor [tolerance=±5% resistance=220 package=THT]
  Stereo = female pin header, 2 pins [form="♀ (female)"]
  9V_DC = female pin header, 2 pins [form="♀ (female)"]

nets:
  N1: Audio_Out.Sleeve, NE556.GND, 10nF.1, 100nF.0, 4_7k.Pin_1, 9V_DC.pin2
  N2: Audio_Out.Ring, Stereo.pin2
  N3: Audio_Out.Tip, 10k.Pin_0, 4_7k.Pin_0, Stereo.pin1
  N4: NE556.DIS, 470k.pin2, 1k.Pin_0
  N5: NE556.THR, NE556.TRIG, 1k.Pin_1, 10nF.0
  N6: NE556.RST, NE556.RST2, NE556.VCC, 470k.pin1, 470k_2.pin1, 9V_DC.pin1
  N7: NE556.OUT, NE556.TRIG2
  N8: NE556.OUT2, 10uF.+
  N9: NE556.THR2, NE556.DIS2, 470k_2.pin2, 100nF.1
  N10: 10uF.-, 10k.Pin_1

notes:
  +
  -
  APC
