# Fritzing sketch Stylophone_singlesided (saved by Fritzing 0.9.3b)
circuit board: 10cm x 7cm
breadboards: 1

parts:
  NE555 = 555 Timer [package="DIP8 [THT]"]
  LM386N = LM 358 Dual Op-Amp [package="DIP8 [THT]"]
  6-12V_DC = Screw terminal - 2 pins [package=THT]
  Audio_Out = Audio Jack (TRS) 3.5mm [package="4Ucon 08780 [THT]"]
  Power_plug2 = Power plug
  Pad1 = Pad [width=2.5 height=30 connect=center]
  Speaker_Out = female pin header, 2 pins [form="♀ (female)"]
  22k = Resistor [tolerance=±5% resistance=220 package=THT]
  2k0 = Resistor [tolerance=±5% resistance=220 package=THT]
  560 = Resistor [tolerance=±5% resistance=220 package=THT]
  Pad2 = Pad [width=7 height=14 connect=center]
  Pad3 = Pad [width=2.5 height=30 connect=center]
  Pad23 = Pad [width=7 height=15 connect=center]
  4k7 = Resistor [tolerance=±5% resistance=220 package=THT]
  4k3 = Resistor [tolerance=±5% resistance=220 package=THT]
  Pad24 = Pad [width=7 height=15 connect=center]
  4k3_2 = Resistor [tolerance=±5% resistance=220 package=THT]
  Pad25 = Pad [width=7 height=14 connect=center]
  Pad26 = Pad [width=2.5 height=30 connect=center]
  Pad27 = Pad [width=7 height=15 connect=center]
  3k9 = Resistor [tolerance=±5% resistance=220 package=THT]
  Pad28 = Pad [width=2.5 height=30 connect=center]
  Pad29 = Pad [width=2.5 height=30 connect=center]
  Pad31 = Pad [width=7 height=14 connect=center]
  Pad32 = Pad [width=4.5 height=14.297260130902881 connect=center]
  Pad33 = Pad [width=7 height=15 connect=center]
  3k6 = Resistor [tolerance=±5% resistance=220 package=THT]
  3k3 = Resistor [tolerance=±5% resistance=220 package=THT]
  Pad35 = Pad [width=7 height=15 connect=center]
  3k0 = Resistor [tolerance=±5% resistance=220 package=THT]
  3k0_2 = Resistor [tolerance=±5% resistance=220 package=THT]
  3k9_2 = Resistor [tolerance=±5% resistance=220 package=THT]
  Pad36 = Pad [width=2.5 height=30 connect=center]
  Pad37 = Pad [width=7 height=14.297260130902881 connect=center]
  Pad38 = Pad [width=7 height=15 connect=center]
  2k7 = Resistor [tolerance=±5% resistance=220 package=THT]
  2k7_2 = Resistor [tolerance=±5% resistance=220 package=THT]
  Pad39 = Pad [width=2.5 height=30 connect=center]
  Pad40 = Pad [width=7 height=15 connect=center]
  2k4 = Resistor [tolerance=±5% resistance=220 package=THT]
  Pad41 = Pad [width=2.5 height=30 connect=center]
  Pad42 = Pad [width=2.5 height=30 connect=center]
  Pad43 = Pad [width=2.5 height=30 connect=center]
  Pad44 = Pad [width=7 height=14 connect=center]
  Pad45 = Pad [width=7 height=14 connect=center]
  Pad46 = Pad [width=7 height=15 connect=center]
  Pad47 = Pad [width=7 height=15 connect=center]
  2k4_2 = Resistor [tolerance=±5% resistance=220 package=THT]
  2k2 = Resistor [tolerance=±5% resistance=220 package=THT]
  Pad48 = Pad [width=7 height=15 connect=center]
  2k2_2 = Resistor [tolerance=±5% resistance=220 package=THT]
  2k0_2 = Resistor [tolerance=±5% resistance=220 package=THT]
  1k8 = Resistor [tolerance=±5% resistance=220 package=THT]
  Pad49 = Pad [width=2.5 height=30 connect=center]
  Pad50 = Pad [width=2.5 height=30 connect=center]
  Pad51 = Pad [width=2.5 height=30 connect=center]
  Pad52 = Pad [width=7 height=14 connect=center]
  Pad53 = Pad [width=4.5 height=14 connect=center]
  Pad54 = Pad [width=7 height=15 connect=center]
  Pad55 = Pad [width=4 height=15 connect=center]
  1k8_2 = Resistor [tolerance=±5% resistance=220 package=THT]
  1k6 = Resistor [tolerance=±5% resistance=220 package=THT]
  Pad56 = Pad [width=7 height=15 connect=center]
  1k5 = Resistor [tolerance=±5% resistance=220 package=THT]
  1k5_2 = Resistor [tolerance=±5% resistance=220 package=THT]
  Stylus = Pad [width=4 height=4 connect=center]
  J4 = female pin header, 1 pin [form="♀ (female)"]
  In- = female pin header, 2 pins [form="♀ (female)"]
  In+ = female pin header, 2 pins [form="♀ (female)"]
  Out- = female pin header, 2 pins [form="♀ (female)"]
  Out+ = female pin header, 2 pins [form="♀ (female)"]
  Vin_select = female pin header, 3 pins [form="♀ (female)"]
  4k7_Pot = female pin header, 3 pins [form="♀ (female)"]
  4k7_2 = Resistor [tolerance=±5% resistance=220 package=THT]
  1k0 = Resistor [tolerance=±5% resistance=220 package=THT]
  3k3_2 = Resistor [tolerance=±5% resistance=220 package=THT]
  33nF = Ceramic Capacitor [capacitance=100nF package="200 mil [THT, multilayer]"]
  100uF = Electrolytic Capacitor [capacitance=1µF package="100 mil [THT, electrolytic]"]
  100nF = Ceramic Capacitor [capacitance=100nF package="200 mil [THT, multilayer]"]
  100nF_2 = Ceramic Capacitor [capacitance=100nF package="200 mil [THT, multilayer]"]
  10kPot = female pin header, 3 pins [form="♀ (female)"]
  100uF_2 = Electrolytic Capacitor [capacitance=1µF package="100 mil [THT, electrolytic]"]
  J5 = double row female pin header, 6 pins [form="♀ (female)"]
  50nF = Ceramic Capacitor [capacitance=100nF package="200 mil [THT, multilayer]"]
  10 = Resistor [tolerance=±5% resistance=220 package=THT]
  2N3904 = NPN-Transistor [package="TO92 [THT]"]
  SW = female pin header, 2 pins [form="♀ (female)"]
  68k = Resistor [tolerance=±5% resistance=220 package=THT]
  100nF_3 = Ceramic Capacitor [capacitance=100nF package="200 mil [THT, multilayer]"]
  10M = Resistor [tolerance=±5% resistance=220 package=THT]
  100nF_4 = Ceramic Capacitor [capacitance=100nF package="200 mil [THT, multilayer]"]
  51k = Resistor [tolerance=±5% resistance=220 package=THT]
  6_8k = Resistor [tolerance=±5% resistance=220 package=THT]
  68k_2 = Resistor [tolerance=±5% resistance=220 package=THT]
  100nF_5 = Ceramic Capacitor [capacitance=100nF package="200 mil [THT, multilayer]"]
  100nF_6 = Ceramic Capacitor [capacitance=100nF package="200 mil [THT, multilayer]"]
  J7 = female pin header, 1 pin [form="♀ (female)"]
  J6 = female pin header, 4 pins [form="♀ (female)"]

nets:
  N1: NE555.Ground, LM386N.connector1, LM386N.connector3, 6-12V_DC.pin1, Audio_Out.Sleeve, Power_plug2.GND, Speaker_Out.pin1, In-.pin1, In-.pin2, Out-.pin1, Out-.pin2, 3k3_2.Pin_0, 33nF.1, 100uF.-, 100nF.0, 10kPot.pin1, 10.Pin_0, 2N3904.E, SW.pin2, 6_8k.Pin_0, 68k_2.Pin_0
  N2: NE555.Trigger, NE555.Threshold, 22k.Pin_1, 33nF.0
  N3: NE555.Output, Stylus.pad, J4.pin1, 100nF_2.1
  N4: NE555.Reset, NE555.Vcc_Supply_Voltage, LM386N.connector5, Vin_select.pin2, 1k0.Pin_0, 68k.Pin_1, J6.pin3
  N5: NE555.Control_Voltage, 4k7_2.Pin_1, 100nF_3.1
  N6: LM386N.connector0, J7.pin1
  N7: LM386N.connector2, 10kPot.pin2
  N8: LM386N.connector4, 100uF_2.+, 50nF.0, J6.pin4
  N9: LM386N.connector6, J6.pin2
  N10: LM386N.connector7, J6.pin1
  N11: 6-12V_DC.pin2, Power_plug2.VCC, In+.pin1, In+.pin2, Vin_select.pin1, 100uF.+, 100nF.1
  N12: Audio_Out.Ring, J5.pin5
  N13: Audio_Out.Tip, J5.pin6
  N14: Pad1.pad, Pad23.pad, 4k7.Pin_0
  N15: Speaker_Out.pin2, J5.pin4
  N16: 22k.Pin_0, 2k0.Pin_1
  N17: 2k0.Pin_0, 560.Pin_1
  N18: 560.Pin_0, Pad51.pad, Pad55.pad, 1k5_2.Pin_1
  N19: Pad2.pad, 4k7.Pin_1, 4k3.Pin_0
  N20: Pad3.pad, 4k3.Pin_1, Pad24.pad, 4k3_2.Pin_0
  N21: 4k3_2.Pin_1, Pad25.pad, 3k9.Pin_0
  N22: Pad26.pad, Pad27.pad, 3k9.Pin_1, 3k9_2.Pin_0
  N23: Pad28.pad, 3k3.Pin_1, Pad35.pad, 3k0.Pin_0
  N24: Pad29.pad, Pad33.pad, 3k6.Pin_0, 3k9_2.Pin_1
  N25: Pad31.pad, 3k6.Pin_1, 3k3.Pin_0
  N26: Pad32.pad, 3k0.Pin_1, 3k0_2.Pin_0
  N27: 3k0_2.Pin_1, Pad36.pad, Pad38.pad, 2k7.Pin_0
  N28: Pad37.pad, 2k7.Pin_1, 2k7_2.Pin_0
  N29: 2k7_2.Pin_1, Pad39.pad, Pad40.pad, 2k4.Pin_0
  N30: 2k4.Pin_1, Pad42.pad, Pad46.pad, 2k4_2.Pin_0
  N31: Pad41.pad, 2k2.Pin_1, Pad48.pad, 2k2_2.Pin_0
  N32: Pad43.pad, Pad47.pad, 2k0_2.Pin_1, 1k8.Pin_0
  N33: Pad44.pad, 2k4_2.Pin_1, 2k2.Pin_0
  N34: Pad45.pad, 2k2_2.Pin_1, 2k0_2.Pin_0
  N35: 1k8.Pin_1, Pad50.pad, Pad54.pad, 1k8_2.Pin_0
  N36: Pad49.pad, 1k6.Pin_1, Pad56.pad, 1k5.Pin_0
  N37: Pad52.pad, 1k8_2.Pin_1, 1k6.Pin_0
  N38: Pad53.pad, 1k5.Pin_1, 1k5_2.Pin_0
  N39: Out+.pin1, Out+.pin2, Vin_select.pin3
  N40: 4k7_Pot.pin1, 3k3_2.Pin_1
  N41: 4k7_Pot.pin2, 4k7_2.Pin_0
  N42: 4k7_Pot.pin3, 1k0.Pin_1
  N43: 100nF_2.0, 10kPot.pin3
  N44: 100uF_2.-, J5.pin1, J5.pin2, J5.pin3
  N45: 50nF.1, 10.Pin_1
  N46: 2N3904.B, 10M.Pin_1, 100nF_6.0
  N47: 2N3904.C, SW.pin1, 68k.Pin_0, 100nF_3.0, 10M.Pin_0, 100nF_4.1
  N48: 100nF_4.0, 51k.Pin_1, 100nF_5.1
  N49: 51k.Pin_0, 6_8k.Pin_1
  N50: 68k_2.Pin_1, 100nF_5.0, 100nF_6.1
